// Logisim project lab4.circ as structural Verilog: 6 circuits, main circuit main
module main (
  input  W,
  input  X,
  input  Y,
  input  Z,
  output D,
  output C,
  output B,
  output A
);

  wire ic7408_1_out_9, ic7408_1_out_10, ic7408_1_out_11, ic7408_1_out_12, ic7408_2_out_9, ic7408_2_out_10,
       ic7411_1_out_10, ic_7404_1_out_8, ic_7404_1_out_9;

  IC_7404 ic_7404_1 (
    .in_1(Z), .in_2(X), .in_3(Y), .out_7(D), .out_8(ic_7404_1_out_8), .out_9(ic_7404_1_out_9));  // open: in_4, in_5, in_6, out_10, out_11, out_12
  IC7408 ic7408_1 (
    .in_1(X), .in_2(Y), .in_3(X), .in_4(Z), .in_5(ic_7404_1_out_8), .in_6(Y), .in_7(ic_7404_1_out_8),
    .in_8(Z), .out_9(ic7408_1_out_9), .out_10(ic7408_1_out_10), .out_11(ic7408_1_out_11),
    .out_12(ic7408_1_out_12));
  IC7411 ic7411_1 (
    .in_1(W), .in_2(ic_7404_1_out_9), .in_3(D), .out_10(ic7411_1_out_10));  // open: in_4, in_5, in_6, in_7, in_8, in_9, out_11, out_12
  IC7408 ic7408_2 (
    .in_1(Y), .in_2(Z), .in_3(D), .in_4(ic_7404_1_out_9), .out_9(ic7408_2_out_9), .out_10(ic7408_2_out_10));  // open: in_5, in_6, in_7, in_8, out_11, out_12
  IC7432 ic7432_1 (
    .in_1(ic7408_2_out_9), .in_2(ic7408_2_out_10), .out_9(C));  // open: in_3, in_4, in_5, in_6, in_7, in_8, out_10, out_11, out_12
  IC_4075 ic_4075_1 (
    .in_4(ic7408_1_out_11), .in_5(ic7408_1_out_12), .in_6(ic7411_1_out_10), .in_7(ic7408_1_out_9),
    .in_8(ic7408_1_out_10), .in_9(W), .out_11(B), .out_12(A));  // open: in_1, in_2, in_3, out_10
endmodule

module IC7411 (
  input  in_1,
  input  in_2,
  input  in_3,
  input  in_4,
  input  in_5,
  input  in_6,
  input  in_7,
  input  in_8,
  input  in_9,
  output out_10,
  output out_11,
  output out_12
);

  and and_1 (out_10, in_1, in_2, in_3);
  and and_2 (out_11, in_4, in_5, in_6);
  and and_3 (out_12, in_7, in_8, in_9);
endmodule

module IC_4075 (
  input  in_1,
  input  in_2,
  input  in_3,
  input  in_4,
  input  in_5,
  input  in_6,
  input  in_7,
  input  in_8,
  input  in_9,
  output out_10,
  output out_11,
  output out_12
);

  or or_1 (out_10, in_1, in_2, in_3);
  or or_2 (out_11, in_4, in_5, in_6);
  or or_3 (out_12, in_7, in_8, in_9);
endmodule

module IC_7404 (
  input  in_1,
  input  in_2,
  input  in_3,
  input  in_4,
  input  in_5,
  input  in_6,
  output out_7,
  output out_8,
  output out_9,
  output out_10,
  output out_11,
  output out_12
);

  not not_1 (out_7, in_1);
  not not_2 (out_8, in_2);
  not not_3 (out_9, in_3);
  not not_4 (out_10, in_4);
  not not_5 (out_11, in_5);
  not not_6 (out_12, in_6);
endmodule

module IC7408 (
  input  in_1,
  input  in_2,
  input  in_3,
  input  in_4,
  input  in_5,
  input  in_6,
  input  in_7,
  input  in_8,
  output out_9,
  output out_10,
  output out_11,
  output out_12
);

  and and_1 (out_9, in_1, in_2);
  and and_2 (out_10, in_3, in_4);
  and and_3 (out_11, in_5, in_6);
  and and_4 (out_12, in_7, in_8);
endmodule

module IC7432 (
  input  in_1,
  input  in_2,
  input  in_3,
  input  in_4,
  input  in_5,
  input  in_6,
  input  in_7,
  input  in_8,
  output out_9,
  output out_10,
  output out_11,
  output out_12
);

  or or_1 (out_9, in_1, in_2);
  or or_2 (out_10, in_3, in_4);
  or or_3 (out_11, in_5, in_6);
  or or_4 (out_12, in_7, in_8);
endmodule
